// Logisim project trabalho1.circ as structural Verilog: 1 circuit, main circuit main
module main (
  input  D,
  input  U,
  input  L
);

  wire and_1_out, and_2_out, not_1_out;

  not not_1 (not_1_out, U);
  and and_1 (and_1_out, D, U);
  and and_2 (and_2_out, D, not_1_out, L);
  LED led_1 (.in(and_1_out));
  LED led_2 (.in(and_2_out));

  // Notes on the sheet:
  //   UP
  //   DOWN
endmodule
